# Fritzing sketch motionSensor_Raspberry (saved by Fritzing 0.9.0b)
breadboards: 1

parts:
  PIR1 = PIR sensor
  Raspberry_Pi_B_rev1 = Raspberry Pi B rev1
  LED3 = LED - 3mm [color="Red (633nm)" package="3 mm [THT]"]
  LED4 = LED - 3mm [color="Green (555nm)" package="3 mm [THT]"]
  R1 = Resistor [tolerance=±5% resistance=1k package=THT]
  R2 = Resistor [tolerance=±5% resistance=1k package=THT]

nets:
  VDD: PIR1.VDD, Raspberry_Pi_B_rev1.5V
  N1: PIR1.SIG, Raspberry_Pi_B_rev1.GPIO_17
  GND: PIR1.GND, Raspberry_Pi_B_rev1.GND, LED3.cathode, LED4.cathode
  N2: Raspberry_Pi_B_rev1.GPIO_23, R1.Pin_0
  N3: Raspberry_Pi_B_rev1.GPIO_24, R2.Pin_0
  N4: LED3.anode, R2.Pin_1
  N5: LED4.anode, R1.Pin_1
